# Fritzing sketch Sketch (saved by Fritzing 1.0.1rc)

parts:
  R1 = Resistor [tolerance=±5% resistance=330 package="2010 [SMD]"]
  C3 = Electrolytic Capacitor [capacitance=1μF voltage=6.3V package="0405 [SMD, electrolytic]"]
  M2 = STM32F103C8T6 blue mini board
  VCC2 = 4 x AAA Battery Mount
  U1 = WS2812 RGB LED strip
  Mod1 = Heltec WiFi LoRa 32 V2 [part_number=HTIT-WB32LA]

nets:
  N1: R1.Pin_0, M2.A1
  N2: R1.Pin_1, U1.DIN
  GND: C3.-, M2.G, VCC2.-, U1.GND, Mod1.GND
  N3: C3.+, VCC2.+, U1.VCC
  N4: M2.A9, Mod1.pin_36
  N5: M2.A10, Mod1.pin_35

custom parts:
  WS2812 RGB LED strip: WS2812 strip
